// Digital circuit test_decode.dig as structural Verilog
module test_decode (
  input  [1:0] IR_Ctrl,
  input  [1:0] Memory_Ctrl,
  input  [3:0] Memory_Input,
  input  [1:0] PC_Ctrl,
  input  Sim_Clk,
  output [1:0] PC_Output,
  output [15:0] Instruction_Out,
  output [1:0] LM_Register,
  output [2:0] Operation,
  output [1:0] M_Register,
  output [1:0] R_Register
);

  // IR_Memory_Module ir_memory_module_1: pin names not known; wires that end beside it: PC_Ctrl, Sim_Clk, Memory_Input, Memory_Ctrl, IR_Ctrl, PC_Output, Instruction_Out

  assign LM_Register = Instruction_Out[5:4];
  assign M_Register = Instruction_Out[3:2];
  assign Operation = Instruction_Out[8:6];
  assign R_Register = Instruction_Out[1:0];

  // Notes on the sheet:
  //   PC_Ctrl: default 1
endmodule

/* Test case:
Sim-Clk IR-Ctrl Memory-Ctrl Memory-Input PC-Ctrl PC-Output Instruction-Out LM-Register M-Register R-Register Operation
c 0 1 0x0 1 x x x x x x 
c 0 1 0x4 1 x x x x x x
c 0 1 0x1 1 x x x x x x
c 0 1 0x0 1 x x x x x x

c 1 0 0x0 1 x x x x x x 
c 1 0 0x4 1 x x x x x x
c 1 0 0x1 1 x x x x x x
c 1 0 0x0 1 x x x x x x

c 1 0 0x0 1 x x x x x x 
c 1 0 0x4 1 x x x x x x
c 1 0 0x1 1 x x x x x x
c 1 0 0x0 1 x x x x x x

c 1 0 0x0 1 x x x x x x 
c 1 0 0x4 1 x x x x x x
c 1 0 0x1 1 x x x x x x
c 1 0 0x0 1 x x x x x x

c 1 0 0x0 1 x x x x x x 
c 1 0 0x4 1 x x x x x x
c 1 0 0x1 1 x x x x x x
c 1 0 0x0 1 x x x x x x
*/
